# Fritzing sketch Assignement3_FAGGIANO_fritzing (saved by Fritzing 0.9.3b)
breadboards: 1

parts:
  Composant3 = Arduino Board Ethernet
  R2 = Resistor [tolerance=±5% resistance=220 package="0805 [SMD]"]

nets:
  N1: Composant3.A0, R2.Pin_1
  N2: Composant3.GND, R2.Pin_0

notes:
  To water cup
  Arduino Ethernet shield containing a 8GB SD card on top of Arduino MEGA card
