# Fritzing sketch Assignement4_FAGGIANO_fritzing (saved by Fritzing 0.9.3b)
breadboards: 1

parts:
  Composant1 = Arduino Board Ethernet
  R1 = Resistor [tolerance=±5% resistance=220 package="0805 [SMD]"]
  Composant2 = Adafruit Bluefruit LE SPI Friend [part_number="Adafruit #2633"]

nets:
  N1: Composant1.D8, Composant2.CS
  N2: Composant1.D11/MOSI, Composant2.MOSI
  N3: Composant1.D12/MISO, Composant2.MISO
  N4: Composant1.D13/SCK, Composant2.SCK
  N5: Composant1.A0, R1.Pin_1
  N6: Composant1.D4, Composant2.RST
  N7: Composant1.D7, Composant2.IRQ
  5V: Composant1.5V, Composant2.VIN
  GND: Composant1.GND, R1.Pin_0, Composant2.GND

notes:
  To water cup
  Arduino Ethernet shield on top of Arduino UNO card

custom parts:
  Adafruit Bluefruit LE SPI Friend: The Bluefruit LE SPI Friend makes it easy to add Bluetooth Low Energy connectivity to anything with 4 or 5 GPIO pins. With SPI, you don't have to worry about baud rates, flow control, or giving up a hardware UART port. Connect to your Arduino or other microcontroller using the common four-pin SPI interface (MISO, MOSI, SCK and CS) plus a 5th GPIO pin for interrupts (to let the Arduino know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
