# Fritzing sketch fianlproject_fritzing_faggiano (saved by Fritzing 0.9.3b)
breadboards: 2

parts:
  Composant1 = Arduino Uno (Rev3)
  S1 = Tilt Switch [package=THT]
  LED1 = LED - 5mm [color="Red (633nm)" package="5 mm [THT]"]
  R1 = Resistor [tolerance=±5% resistance=220 package=THT]
  Composant3 = Adafruit Bluefruit LE SPI Friend [part_number="Adafruit #2633"]
  U2 = LCD-16X2 [package=lcd-16x2]
  R5 = Resistor [tolerance=±5% resistance=10k package="0603 [SMD]"]
  R6 = Trimmer Potentiometer [maximum_resistance=10kΩ package=THT]
  S2 = Pushbutton [package="[THT]"]
  R7 = Resistor [tolerance=±5% resistance=10k package=THT]

nets:
  N1: Composant1.A0, R1.Pin_0
  N2: Composant1.A2, S2.Pin_1, S2.Pin_2, R7.Pin_0
  N3: Composant1.D8, Composant3.CS
  N4: Composant1.D9_PWM, U2.E
  N5: Composant1.D10_PWM/SS, U2.RS
  N6: Composant1.D11_PWM/MOSI, Composant3.MOSI
  N7: Composant1.D12/MISO, Composant3.MISO
  N8: Composant1.D13/SCK, Composant3.SCK
  N9: Composant1.D2, S1.Pin_2
  N10: Composant1.D3_PWM, U2.DB4
  N11: Composant1.D4, U2.DB5
  N12: Composant1.D5_PWM, U2.DB6
  N13: Composant1.D6_PWM, U2.DB7
  N14: Composant1.D7, Composant3.IRQ
  5V: Composant1.5V, Composant3.VIN, U2.VDD, U2.K, R6.leg2, S2.Pin_3, S2.Pin_4
  GND: Composant1.GND, S1.Pin_1, LED1.cathode, Composant3.GND, U2.VSS, U2.R_W, R5.Pin_0, R6.leg1, R7.Pin_1
  N15: LED1.anode, R1.Pin_1
  N16: U2.VO, R6.wiper
  N17: U2.A, R5.Pin_1

custom parts:
  Adafruit Bluefruit LE SPI Friend: The Bluefruit LE SPI Friend makes it easy to add Bluetooth Low Energy connectivity to anything with 4 or 5 GPIO pins. With SPI, you don't have to worry about baud rates, flow control, or giving up a hardware UART port. Connect to your Arduino or other microcontroller using the common four-pin SPI interface (MISO, MOSI, SCK and CS) plus a 5th GPIO pin for interrupts (to let the Arduino know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
