# Fritzing sketch faggiano-anais-assignement-2 (saved by Fritzing 0.9.3b)
breadboards: 3

parts:
  Composant1 = Arduino Uno (Rev3) - ICSP
  LED1 = smd LED [color="Blue (430nm)" package="0805 [SMD]"]
  LED2 = smd LED [color="White (4500K)" package="0805 [SMD]"]
  LED3 = smd LED [color="Red (660nm)" package="0805 [SMD]"]
  LED4 = smd LED [color="Green (555nm)" package="0805 [SMD]"]
  U1 = LCD-16X2 [package=lcd-16x2]
  R1 = Resistor [tolerance=±5% resistance=10k package="0603 [SMD]"]
  R2 = Trimmer Potentiometer [maximum_resistance=10kΩ package=THT]
  S1 = Pushbutton [package=THT]
  R3 = Resistor [tolerance=±5% resistance=10k package="0603 [SMD]"]
  J1 = Basic Force Sensing Resistor (FSR) [package=THT]
  J2 = Basic Force Sensing Resistor (FSR) [package=THT]
  J3 = Basic Force Sensing Resistor (FSR) [package=THT]
  J4 = Basic Force Sensing Resistor (FSR) [package=THT]
  R4 = Resistor [tolerance=±5% resistance=10k package=THT]
  R5 = Resistor [tolerance=±5% resistance=10k package=THT]
  R7 = Resistor [tolerance=±5% resistance=10k package=THT]
  R8 = Resistor [tolerance=±5% resistance=10k package=THT]
  J5 = Piezo Speaker
  R9 = Resistor [tolerance=±5% resistance=10k package=THT]

nets:
  N1: Composant1.A0, J4.pin_0, R5.Pin_0
  N2: Composant1.A1, J3.pin_0, R4.Pin_0
  N3: Composant1.A2, J2.pin_0, R8.Pin_0
  N4: Composant1.A3, J1.pin_0, R7.Pin_0
  N5: Composant1.A4/SDA, R9.Pin_0
  N6: Composant1.D8, U1.RS
  N7: Composant1.D9_PWM, LED4.anode
  N8: Composant1.D10_PWM/SS, LED3.anode
  N9: Composant1.D11_PWM/MOSI, LED1.anode
  N10: Composant1.D12/MISO, LED2.anode
  GND: Composant1.GND, LED1.cathode, LED2.cathode, LED3.cathode, LED4.cathode, U1.VSS, U1.R_W, U1.K, R1.Pin_0, R2.leg1, R3.Pin_1, R4.Pin_1, R5.Pin_1, R7.Pin_1, R8.Pin_1, J5.pin1
  N11: Composant1.D2, S1.leg0, R3.Pin_0
  N12: Composant1.D3_PWM, U1.DB7
  N13: Composant1.D4, U1.DB6
  N14: Composant1.D5_PWM, U1.DB5
  N15: Composant1.D6_PWM, U1.DB4
  N16: Composant1.D7, U1.E
  5V: Composant1.5V, U1.VDD, R2.leg2, S1.leg1, J1.pin_1, J2.pin_1, J3.pin_1, J4.pin_1
  N17: U1.VO, R2.wiper
  N18: U1.A, R1.Pin_1
  N19: J5.pin2, R9.Pin_1
